# Fritzing sketch vsensor-veroboard (saved by Fritzing 0.9.3b)
circuit board: 8.46667cm x 5.64444cm
stripboards: 1

parts:
  Part1 = Arduino Nano (Rev3.0)
  J1 = screw terminal, 2 pins
  R1 = Resistor [tolerance=±5% resistance=10k package="2512 [SMD]"]
  R2 = Resistor [tolerance=±5% resistance=1.8k package="2512 [SMD]"]
  SSR = G3VM-61E1 [package=g3vm-61e1]
  J3 = screw terminal, 2 pins

nets:
  N1: Part1.GND, R2.Pin_0, SSR.P$4
  N2: Part1.D5, SSR.P$6
  N3: Part1.5V, SSR.P$5
  N4: Part1.A1, J1.pin1, J1.pin2, R1.Pin_1, R2.Pin_1
  N5: SSR.P$2, J3.pin2
  N6: SSR.P$3, J3.pin1

notes:
  24V sense
  +
  -
  passive switch
  trigger
  common
  N/O
  N/C
  voltage sense
  relay trigger
